# Fritzing sketch ESP8266_DMXController_Prototype (saved by Fritzing 0.9.3b)

parts:
  U1 = MAX485 [package=dil08]
  MCU = NodeMCU V1.0
  XLR1 = XLR3_NCFAH2 [package=xlr3_nc3fah2]

nets:
  VCC: U1.DE, U1.VCC, MCU.3V3
  N1: U1.DI, MCU.D4
  GND: U1.GND, MCU.GND, XLR1.1
  N2: U1.A, XLR1.3
  N3: U1.B, XLR1.2

custom parts:
  NodeMCU V1.0: ESP8266 based NodeMCU
